# Fritzing sketch breadboard-wiring (saved by Fritzing 0.9.3b)
breadboards: 1

parts:
  Part2 = Tessel 2
  R1 = Resistor [tolerance=±5% resistance=100 package="2512 [SMD]"]
  R2 = Resistor [tolerance=±5% resistance=100 package="2512 [SMD]"]
  R3 = Resistor [tolerance=±5% resistance=100 package="2512 [SMD]"]
  R4 = Resistor [tolerance=±5% resistance=100 package="2512 [SMD]"]
  LED1 = LED - 5mm [color="Green (555nm)" package="5 mm [THT]"]
  LED2 = LED - 5mm [color="Red (633nm)" package="5 mm [THT]"]
  LED3 = LED - 5mm [color="Red (633nm)" package="5 mm [THT]"]
  LED4 = LED - 5mm [color="Orange (612nm)" package="5 mm [THT]"]
  R5 = Resistor [tolerance=±5% resistance=10k package=THT]
  S1 = Momentary Switch [package=ksa_sealed_tac_switch]

nets:
  N1: Part2.3, R1.Pin_1
  N2: Part2.4, R2.Pin_1
  N3: Part2.5, R3.Pin_1
  N4: Part2.6, R4.Pin_1
  N5: Part2.7, R5.Pin_0, S1.2
  N6: Part2.3V3, S1.4
  N7: R1.Pin_0, LED1.anode
  N8: R2.Pin_0, LED2.anode
  N9: R3.Pin_0, LED3.anode
  N10: R4.Pin_0, LED4.anode
  N11: LED1.cathode, LED2.cathode, LED3.cathode, LED4.cathode, R5.Pin_1

custom parts:
  Tessel 2: Draft version of Tessel 2
